# Fritzing sketch talkingD20 (saved by Fritzing 1.0.0d)

parts:
  Part1 = Adafruit Audio FX Mini Sound Board [part_number="Adafruit #2342 and #2220"]
  Part2 = Adafruit Feather nRF52840 Sense [part_number="Adafruit #4516"]
  Part3 = Adafruit PAM8302 [part_number="Adafruit #2130"]
  SP1 = SPEAKER [package=pcb_mount_speaker]

nets:
  GND: Part1.GND, Part2.GND, Part3.GND, Part3.AIN-
  N1: Part1.RST, Part2.SCK
  VIN: Part1.VIN, Part2.3.3V, Part3.VCC
  N2: Part1.TX, Part2.TX
  N3: Part1.RX_5V, Part2.RX
  N4: Part1.R_AC, Part3.AIN+
  N5: Part3.VO+, SP1.+
  N6: Part3.VO-, SP1.-

notes:
  Note, I did not actually connect that pin to SCK but to GPIO 8 which is the same as SCK in the pinout

custom parts:
  Adafruit Audio FX Mini Sound Board: Would you like to add audio/sound effects to your next project, without an Arduino+Shield? Or maybe you don't even know how to use microcontrollers, you just want to make a sound play whenever you press a button. What about something that has to be very small and portable? You are probably feeling a little frustrated: it's been very hard to find a simple, low cost audio effects trigger that is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
  Adafruit Feather nRF52840 Sense: The Adafruit Feather Bluefruit Sense takes our popular Feather nRF52840 Express and adds a smorgasbord of sensors to make a great wireless sensor platform. This Feather microcontroller comes with Bluetooth Low Energy and native USB support featuring the nRF52840! This Feather is an 'all-in-one' Arduino-compatible + Bluetooth Low Energy with built in USB plus battery charging. With native USB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
  Adafruit PAM8302: This super small mono amplifier is surprisingly powerful - able to deliver up to 2.5 Watts into 4-8 ohm impedance speakers. Inside the miniature chip is a class D controller, able to run from 2.0V-5.5VDC. Since the amp is a class D, its very efficient (over 90% efficient when driving an 8Ω speaker at over half a Watt) - making it perfect for portable and battery-powered projects. It has built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
